// Logisim project Project1Given.circ as structural Verilog: 4 circuits, main circuit main
module main (
  input  in_1,
  input  in_2,
  input  in_3,
  input  in_4,
  input  Five,
  output N,
  output E,
  output [3:0] out_8
);

  wire fiveseven_1_a, fiveseven_1_b, fiveseven_1_c, fiveseven_1_d, fiveseven_1_e, fiveseven_1_f,
       fiveseven_1_g;

  Compare compare_1 (.X0(1'b1), .X1(1'b1), .X2(1'b1), .Y0(1'b1), .Y1(1'b1), .Y2(1'b1), .N(N), .E(E));
  Gray gray_1 (.B0(1'b1), .B1(1'b1), .B2(1'b0), .B3(1'b0), .G0(out_8[0]), .G1(out_8[1]), .G2(out_8[2]), .G3(out_8[3]));
  FiveSeven fiveseven_1 (
    .V(in_1), .W(in_2), .X(in_3), .Y(in_4), .Z(Five), .A(fiveseven_1_a), .B(fiveseven_1_b),
    .C(fiveseven_1_c), .D(fiveseven_1_d), .E(fiveseven_1_e), .F(fiveseven_1_f), .G(fiveseven_1_g));
  _7_Segment_Display u_7_segment_display_1 (
    .g(fiveseven_1_g), .f(fiveseven_1_f), .a(fiveseven_1_a), .b(fiveseven_1_b), .e(fiveseven_1_e),
    .d(fiveseven_1_d), .c(fiveseven_1_c));  // open: dp
endmodule

module Compare (
  input  X0,
  input  X1,
  input  X2,
  input  Y0,
  input  Y1,
  input  Y2,
  output N,
  output E
);

  wire and_1_out, and_2_out, and_3_out, E0, E1, E2;

  xnor xnor_1 (E0, X0, Y0);
  xnor xnor_2 (E1, X1, Y1);
  xnor xnor_3 (E2, X2, Y2);
  and and_1 (and_1_out, ~X1, E1, E1, Y1);  // AND_Gate
  and and_2 (and_2_out, ~X1, E2, Y1);  // AND_Gate
  and and_3 (and_3_out, ~X2, Y2);  // AND_Gate
  and and_4 (E, E0, E1, E2);
  or or_1 (N, and_1_out, and_2_out, and_3_out);
endmodule

module Gray (
  input  B0,
  input  B1,
  input  B2,
  input  B3,
  output G0,
  output G1,
  output G2,
  output G3
);

  wire and_1_out, and_2_out, and_3_out, and_4_out, and_5_out, and_6_out, and_7_out, and_8_out, and_9_out,
       and_10_out, and_11_out, NotB0, NotB2, NotB3;

  not not_1 (NotB0, B0);
  not not_2 (G0, B1);
  not not_3 (NotB2, B2);
  not not_4 (NotB3, B3);
  and and_1 (and_1_out, NotB2, B0);
  and and_2 (and_2_out, NotB2, B1);
  and and_3 (and_3_out, B2, G0, NotB0);
  or or_1 (G1, and_1_out, and_2_out, and_3_out);
  and and_4 (and_4_out, B3, B2);
  and and_5 (and_5_out, B3, B1, B0);
  and and_6 (and_6_out, NotB3, NotB2, G0);
  and and_7 (and_7_out, NotB3, NotB2, NotB0);
  or or_2 (G2, and_4_out, and_5_out, and_6_out, and_7_out);
  and and_8 (and_8_out, NotB3, G0);
  and and_9 (and_9_out, NotB3, NotB2);
  and and_10 (and_10_out, NotB3, B1, NotB0);
  and and_11 (and_11_out, B3, B2, B1, B0);
  or or_3 (G3, and_8_out, and_9_out, and_10_out, and_11_out);

  // Other names for the same wires on the sheet: NotB1 = G0
endmodule

module FiveSeven (
  input  V,
  input  W,
  input  X,
  input  Y,
  input  Z,
  output A,
  output B,
  output C,
  output D,
  output E,
  output F,
  output G
);

  wire and_1_out, and_2_out, and_3_out, and_4_out, and_5_out, and_6_out, and_7_out, and_8_out, and_9_out,
       and_10_out, and_11_out, and_12_out, and_13_out, and_14_out, Eight, Five, Four, Nine, One, Seven, Six,
       Three, Two, VFour, VOne, VThree, VTwo, Zero;

  and and_1 (and_1_out, V, ~W, ~X, ~Y);  // AND_Gate
  and and_2 (and_2_out, ~V, W, ~X, ~Y);  // AND_Gate
  and and_3 (and_3_out, ~V, ~W, X, ~Y);  // AND_Gate
  and and_4 (and_4_out, ~V, ~W, ~X, Y);  // AND_Gate
  and and_5 (and_5_out, V, W, ~X, ~Y);  // AND_Gate
  and and_6 (and_6_out, V, ~W, X, ~Y);  // AND_Gate
  and and_7 (and_7_out, V, ~W, ~X, Y);  // AND_Gate
  and and_8 (and_8_out, ~V, W, X, ~Y);  // AND_Gate
  and and_9 (and_9_out, ~V, W, ~X, Y);  // AND_Gate
  and and_10 (and_10_out, ~V, ~W, X, Y);  // AND_Gate
  and and_11 (and_11_out, V, W, X, ~Y);  // AND_Gate
  and and_12 (and_12_out, V, W, ~X, Y);  // AND_Gate
  and and_13 (and_13_out, V, ~W, X, Y);  // AND_Gate
  and and_14 (and_14_out, ~V, W, X, Y);  // AND_Gate
  and and_15 (VFour, V, W, X, Y);
  or or_1 (VOne, and_1_out, and_2_out, and_3_out, and_4_out);
  or or_2 (VTwo, and_5_out, and_6_out, and_7_out, and_8_out, and_9_out, and_10_out);
  or or_3 (VThree, and_11_out, and_12_out, and_13_out, and_14_out);
  and and_16 (One, ~Z, VOne);  // AND_Gate
  and and_17 (Two, ~Z, VTwo);  // AND_Gate
  and and_18 (Three, ~Z, VThree);  // AND_Gate
  and and_19 (Four, ~Z, VFour);  // AND_Gate
  and and_20 (Six, Z, VOne);
  and and_21 (Seven, Z, VTwo);
  and and_22 (Eight, Z, VThree);
  and and_23 (Nine, Z, VFour);
  and and_24 (Five, Z, ~VOne, ~VTwo, ~VThree, ~VFour);  // AND_Gate
  and and_25 (Zero, ~Z, ~VOne, ~VTwo, ~VThree, ~VFour);  // AND_Gate
  or or_4 (A, Two, Three, Five, Six, Seven, Eight, Nine, Zero);
  or or_5 (B, One, Two, Three, Four, Seven, Eight, Nine, Zero);
  or or_6 (C, One, Three, Four, Five, Six, Seven, Eight, Nine, Zero);
  or or_7 (E, Two, Six, Eight, Zero);
  or or_8 (F, Four, Five, Six, Seven, Eight, Nine, Zero);
  or or_9 (D, Two, Three, Five, Six, Eight, Nine, Zero);
  or or_10 (G, Two, Three, Four, Five, Six, Eight, Nine);
endmodule
